# Fritzing sketch schema (saved by Fritzing 1.0.4)

parts:
  A1 = Esp32-c3 super mini
  S1 = 0.91 inch OLED I2C Display 128 x 32 Pixels
  Rotary_Encoder1 = IDUINO Rotary Encoder SE055
  Part1 = Adafruit MAX9814 Electret Microphone Amplifier [part_number="Adafruit #1713"]
  J1 = Piezo Speaker
  U1 = WS2812 RGB LED strip
  C1 = Capacitor Polarized [part_number=470mF package=cpol-radial-100uf-25v]
  Part2 = Adafruit USB Type C Breakout [part_number=4090]
  D1 = Rectifier Diode 10A [part_number=1N4001-1N4007]
  R1 = Resistor [tolerance=±5% power=0.25W resistance=470 package=THT]

nets:
  N1: A1.Pin_1, Rotary_Encoder1.CLK
  N2: A1.Pin_2, Rotary_Encoder1.DT
  N3: A1.Pin_3, Rotary_Encoder1.SW
  N4: A1.Pin_4, S1.SDA
  N5: A1.Pin_5, S1.SCL
  N6: A1.Pin_9, Part1.OUTPUT
  N7: A1.Pin_10, J1.pin2
  N8: A1.Pin_11, R1.Pin_0
  VDD: A1.Pin_14, S1.VCC, Rotary_Encoder1.VDD, Part1.VDD
  GND: A1.Pin_15, S1.GND, Rotary_Encoder1.GND, Part1.GND, J1.pin1, U1.GND, C1.-, Part2.GND
  N9: A1.Pin_16, D1.cathode
  N10: U1.VCC, C1.+, Part2.VBUS, D1.anode
  N11: U1.DIN, R1.Pin_1

custom parts:
  Esp32-c3 super mini: ESP32-C3 Development Board ESP32 SuperMini Development Board ESP32 Development Board WiFi Bluetooth.
  IDUINO Rotary Encoder SE055: https://www.conrad.com/p/iduino-rotary-encoder-1-pcs-se055-1485328
  Adafruit MAX9814 Electret Microphone Amplifier: Add an ear to your project with this well-designed electret microphone amplifier with AGC. This fully assembled and tested board comes with a 20-20KHz electret microphone soldered on. For the amplification, we use the Maxim MAX9814, a specialty chip that is designed for amplifying electret microphones in situations where the loudness of the audio isn't predictable. This fancy microphone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
  WS2812 RGB LED strip: WS2812 strip
  Adafruit USB Type C Breakout: Adafruit breakout board for USB Type C socket.
